// Digital circuit sch3.dig as structural Verilog
module sch3 (
  input  A,
  input  B,
  input  C,
  output Y
);

  wire not_1_out, or_1_out;

  not not_1 (not_1_out, A);
  or or_1 (or_1_out, not_1_out, B);
  or or_2 (Y, or_1_out, C);

  // Notes on the sheet:
  //   ~A | B | C
endmodule
