// Digital circuit sch4.dig as structural Verilog
module sch4 (
  input  A,
  input  B,
  input  C,
  input  D,
  output Y
);

  wire and_1_out, not_1_out, not_2_out, or_1_out;

  not not_1 (not_1_out, A);
  not not_2 (not_2_out, C);
  and and_1 (and_1_out, B, not_2_out);
  or or_1 (or_1_out, not_1_out, and_1_out);
  or or_2 (Y, or_1_out, D);

  // Notes on the sheet:
  //   ~A | (B & ~C)  | D
endmodule
